// Logisim project Control_Unit.circ as structural Verilog: 7 circuits, main circuit Control Unit
module Control_Unit (
  input  END_CS_IN,
  input  RST,
  input  CLK,
  input  [5:0] Func_Code,
  input  [5:0] OP_Code,
  input  Flag,
  output Write_ID,
  output [3:0] ALU_SEL,
  output A_SEL,
  output [1:0] B_SEL,
  output [2:0] RF_Input,
  output [1:0] RF_SEL,
  output [1:0] BC_SEL,
  output [2:0] FLAG_SEL,
  output WRITE_RF,
  output WRITE_PC,
  output Unsigned,
  output DOut_SEL,
  output [1:0] MA_SEL,
  output CS_EN,
  output TTY_EN,
  output RAM_RW,
  output DIn_SEL,
  output Halt,
  output KBD_EN
);

  wire _1_CYCLE_2_q, _1_CYCLE_3_q, _1_CYCLE_q, add, addi, ALUA_SEL_Imm, \and , andi, beq, bgtz, blez, bltz,
       bne, branch, CS_In_Instruction, demultiplexer_1_out1, demultiplexer_2_out1, div, divu, IDLE_q,
       immediate, jr, mfhi, mflo, mul, mulu, \nor , not_1_out, \or , or_1_out, ori, slt, slti, sltiu, sltu,
       Start_Immediate_q, StartZero_q, stImm, stZero, sub, Unsigned_t, WAIT_READ_2_q, WAIT_READ_q,
       WRITE_RF_Imm, WRITE_RF_Zero, WritePC_Imm, WritePC_Zero, \xor , xori, zero;
  wire [1:0] ALUB_SEL_Imm, BC_SEL_Imm, BC_SEL_Zero, RF_SEL_Imm, RF_SEL_Zero;
  wire [2:0] Flag_SEL_t, RF_Input_Imm, RF_Input_Zero;
  wire [3:0] ALU_SEL_Imm, ALU_SEL_Zero;

  Op_Code_Decoder op_code_decoder_1 (
    .o0(OP_Code[0]), .o1(OP_Code[1]), .o2(OP_Code[2]), .o3(OP_Code[3]), .o4(OP_Code[4]), .o5(OP_Code[5]),
    .zero(zero), .beq(beq), .addi(addi), .bne(bne), .andi(andi), .blez(blez), .ori(ori), .bgtz(bgtz),
    .xori(xori), .slti(slti), .sltiu(sltiu), .bltz(bltz), .ENABLE(1'b1));  // open: special, lw, sw, stack
  Func_Code_Decoder func_code_decoder_1 (
    .f0(Func_Code[0]), .f1(Func_Code[1]), .f2(Func_Code[2]), .f3(Func_Code[3]), .f4(Func_Code[4]),
    .f5(Func_Code[5]), .EN(1'b1), .add(add), .\and (\and ), .sub(sub), .\or (\or ), .mul(mul), .\nor (\nor ),
    .mulu(mulu), .\xor (\xor ), .div(div), .mfhi(mfhi), .mflo(mflo), .divu(divu), .slt(slt), .jr(jr),
    .sltu(sltu));  // open: nop_pop, push_tty, halt, rnd, kbd, zero
  Demultiplexer demultiplexer_1 (
    .out0(CS_In_Instruction), .out1(demultiplexer_1_out1), .in(IDLE_q), .sel(RST));  // open: en
  D_Flip_Flop IDLE (.clk(CLK), .D(demultiplexer_1_out1), .Q(IDLE_q), .preset(RST));  // open: Qn, en, reset
  D_Flip_Flop StartZero (.clk(CLK), .D(stZero), .Q(StartZero_q), .reset(RST));  // open: Qn, preset, en
  D_Flip_Flop Start_Immediate (.clk(CLK), .D(stImm), .Q(Start_Immediate_q), .reset(RST));  // open: Qn, preset, en
  or or_1 (or_1_out, CS_In_Instruction, WAIT_READ_q);
  Demultiplexer demultiplexer_2 (
    .out0(Write_ID), .out1(demultiplexer_2_out1), .in(or_1_out), .sel(not_1_out));  // open: en
  or or_2 (immediate, addi, andi, ori, xori, slti, sltiu);
  not not_1 (not_1_out, END_CS_IN);
  D_Flip_Flop WAIT_READ (.clk(CLK), .D(demultiplexer_2_out1), .Q(WAIT_READ_q), .reset(RST));  // open: Qn, preset, en
  ZeroMapper zeromapper_1 (
    .EN(StartZero_q), .add(add), .sub(sub), .mul(mul), .mulu(mulu), .div(div), .divu(divu), .\and (\and ),
    .\or (\or ), .\nor (\nor ), .\xor (\xor ), .mfhi(mfhi), .mflo(mflo), .jr(jr), .slt(slt), .sltu(sltu),
    .WritePC(WritePC_Zero), .ALU_SEL(ALU_SEL_Zero), .WriteRF(WRITE_RF_Zero), .RFInput(RF_Input_Zero),
    .Unsigned(Unsigned_t), .RFSelector(RF_SEL_Zero), .BC_SEL(BC_SEL_Zero));
  D_Flip_Flop _1_CYCLE (.clk(CLK), .D(Start_Immediate_q), .Q(_1_CYCLE_q), .reset(RST));  // open: Qn, preset, en
  I_Mapper i_mapper_1 (
    .EN(Start_Immediate_q), .addi(addi), .andi(andi), .ori(ori), .xori(xori), .slti(slti), .sltiu(sltiu),
    .WritePC(WritePC_Imm), .WriteRF(WRITE_RF_Imm), .ALUA(ALUA_SEL_Imm), .ALUB(ALUB_SEL_Imm),
    .RF_INPUT(RF_Input_Imm), .RF_SEL(RF_SEL_Imm), .BC_SEL(BC_SEL_Imm), .ALU_SEL(ALU_SEL_Imm));
  D_Flip_Flop WAIT_READ_2 (.clk(CLK), .D(Write_ID), .Q(WAIT_READ_2_q), .reset(RST));  // open: Qn, preset, en
  D_Flip_Flop _1_CYCLE_2 (.clk(CLK), .D(StartZero_q), .Q(_1_CYCLE_2_q), .reset(RST));  // open: Qn, preset, en
  and and_1 (stZero, WAIT_READ_2_q, zero);
  and and_2 (stImm, WAIT_READ_2_q, immediate);
  D_Flip_Flop u_Branch (.clk(CLK), .D(branch), .reset(RST));  // open: Q, Qn, preset, en
  or or_3 (branch, beq, bne, blez, bgtz, bltz);
  Branch_Mapper branch_mapper_1 (.beq(beq), .bne(bne), .blez(blez), .bgtz(bgtz), .bltz(bltz), .Flag_Sel(Flag_SEL_t));
  D_Flip_Flop _1_CYCLE_3 (.clk(CLK), .Q(_1_CYCLE_3_q), .reset(RST));  // open: D, Qn, preset, en
endmodule

module Op_Code_Decoder (
  input  o0,
  input  o1,
  input  o2,
  input  o3,
  input  o4,
  input  o5,
  input  ENABLE,
  output zero,
  output beq,
  output stack,
  output addi,
  output bne,
  output special,
  output andi,
  output blez,
  output ori,
  output bgtz,
  output xori,
  output bltz,
  output slti,
  output lw,
  output sltiu,
  output sw
);

  wire and_1_out, and_2_out, and_3_out, and_4_out, and_5_out, and_6_out, and_7_out, and_15_out, and_16_out,
       and_17_out, and_18_out, and_19_out, and_20_out, and_21_out, and_29_out, and_30_out;

  and and_1 (and_1_out, ~o0, ~o1, ~o1, ~o3, ~o4, ~o5);  // AND_Gate
  and and_2 (and_2_out, ~o0, ~o1, ~o1, o3, ~o4, ~o5);  // AND_Gate
  and and_3 (and_3_out, ~o0, ~o1, o1, o3, ~o4, ~o5);  // AND_Gate
  and and_4 (and_4_out, o0, ~o1, o1, o3, ~o4, ~o5);  // AND_Gate
  and and_5 (and_5_out, ~o0, o1, o1, o3, ~o4, ~o5);  // AND_Gate
  and and_6 (and_6_out, ~o0, o1, ~o1, o3, ~o4, ~o5);  // AND_Gate
  and and_7 (and_7_out, o0, o1, ~o1, o3, ~o4, ~o5);  // AND_Gate
  and and_8 (zero, and_1_out, ENABLE);
  and and_9 (addi, and_2_out, ENABLE);
  and and_10 (andi, and_3_out, ENABLE);
  and and_11 (ori, and_4_out, ENABLE);
  and and_12 (xori, and_5_out, ENABLE);
  and and_13 (slti, and_6_out, ENABLE);
  and and_14 (sltiu, and_7_out, ENABLE);
  and and_15 (and_15_out, ~o0, ~o1, o1, ~o3, ~o4, ~o5);  // AND_Gate
  and and_16 (and_16_out, o0, ~o1, o1, ~o3, ~o4, ~o5);  // AND_Gate
  and and_17 (and_17_out, ~o0, o1, o1, ~o3, ~o4, ~o5);  // AND_Gate
  and and_18 (and_18_out, o0, o1, o1, ~o3, ~o4, ~o5);  // AND_Gate
  and and_19 (and_19_out, o0, ~o1, ~o1, ~o3, ~o4, ~o5);  // AND_Gate
  and and_20 (and_20_out, o0, o1, ~o1, ~o3, ~o4, o5);  // AND_Gate
  and and_21 (and_21_out, o0, o1, ~o1, o3, ~o4, o5);  // AND_Gate
  and and_22 (beq, and_15_out, ENABLE);
  and and_23 (bne, and_16_out, ENABLE);
  and and_24 (blez, and_17_out, ENABLE);
  and and_25 (bgtz, and_18_out, ENABLE);
  and and_26 (bltz, and_19_out, ENABLE);
  and and_27 (lw, and_20_out, ENABLE);
  and and_28 (sw, and_21_out, ENABLE);
  and and_29 (and_29_out, ~o0, ~o1, ~o1, o3, o4, o5);  // AND_Gate
  and and_30 (and_30_out, o0, o1, o1, o3, o4, o5);
  and and_31 (stack, and_29_out, ENABLE);
  and and_32 (special, and_30_out, ENABLE);

  assign o2 = o1;

  // Other names for the same wires on the sheet: EN = ENABLE
endmodule

module Func_Code_Decoder (
  input  f0,
  input  f1,
  input  f2,
  input  f3,
  input  f4,
  input  f5,
  input  EN,
  input  zero,
  output add,
  output \and ,
  output nop_pop,
  output sub,
  output \or ,
  output push_tty,
  output mul,
  output \nor ,
  output halt,
  output mulu,
  output \xor ,
  output rnd,
  output kbd,
  output div,
  output mfhi,
  output mflo,
  output divu,
  output slt,
  output jr,
  output sltu
);

  wire and_1_out, and_2_out, and_3_out, and_4_out, and_5_out, and_6_out, and_7_out, and_8_out, and_17_out,
       and_18_out, and_19_out, and_20_out, and_21_out, and_22_out, and_23_out, and_31_out, and_32_out,
       and_33_out, and_34_out, and_35_out;

  and and_1 (and_1_out, ~f0, ~f1, ~f2, ~f3, ~f4, f5);  // AND_Gate
  and and_2 (and_2_out, ~f0, f1, ~f2, ~f3, ~f4, f5);  // AND_Gate
  and and_3 (and_3_out, ~f0, ~f1, ~f2, f3, f4, ~f5);  // AND_Gate
  and and_4 (and_4_out, f0, ~f1, ~f2, f3, f4, ~f5);  // AND_Gate
  and and_5 (and_5_out, ~f0, f1, ~f2, f3, f4, ~f5);  // AND_Gate
  and and_6 (and_6_out, f0, f1, ~f2, f3, f4, ~f5);  // AND_Gate
  and and_7 (and_7_out, ~f0, f1, ~f2, f3, ~f4, f5);  // AND_Gate
  and and_8 (and_8_out, f0, f1, ~f2, f3, ~f4, f5);  // AND_Gate
  and and_9 (add, zero, and_1_out, EN);
  and and_10 (sub, zero, and_2_out, EN);
  and and_11 (mul, zero, and_3_out, EN);
  and and_12 (mulu, zero, and_4_out, EN);
  and and_13 (div, zero, and_5_out, EN);
  and and_14 (divu, zero, and_6_out, EN);
  and and_15 (slt, zero, and_7_out, EN);
  and and_16 (sltu, zero, and_8_out, EN);
  and and_17 (and_17_out, ~f0, ~f1, f2, ~f3, ~f4, f5);  // AND_Gate
  and and_18 (and_18_out, f0, ~f1, f2, ~f3, ~f4, f5);  // AND_Gate
  and and_19 (and_19_out, f0, f1, f2, ~f3, ~f4, f5);  // AND_Gate
  and and_20 (and_20_out, ~f0, ~f1, ~f2, f3, ~f4, f5);  // AND_Gate
  and and_21 (and_21_out, ~f0, ~f1, ~f2, ~f3, f4, ~f5);  // AND_Gate
  and and_22 (and_22_out, ~f0, f1, ~f2, ~f3, f4, ~f5);  // AND_Gate
  and and_23 (and_23_out, ~f0, ~f1, ~f2, f3, ~f4, ~f5);  // AND_Gate
  and and_24 (\and , zero, and_17_out, EN);
  and and_25 (\or , zero, and_18_out, EN);
  and and_26 (\nor , zero, and_19_out, EN);
  and and_27 (\xor , zero, and_20_out, EN);
  and and_28 (mfhi, zero, and_21_out, EN);
  and and_29 (mflo, zero, and_22_out, EN);
  and and_30 (jr, zero, and_23_out, EN);
  and and_31 (and_31_out, ~f0, ~f1, ~f2, ~f3, ~f4, ~f5);  // AND_Gate
  and and_32 (and_32_out, f0, ~f1, ~f2, ~f3, ~f4, ~f5);  // AND_Gate
  and and_33 (and_33_out, f0, f1, f2, f3, f4, f5);
  and and_34 (and_34_out, ~f0, f1, ~f2, ~f3, ~f4, ~f5);  // AND_Gate
  and and_35 (and_35_out, ~f0, ~f1, f2, ~f3, ~f4, ~f5);  // AND_Gate
  and and_36 (nop_pop, and_31_out, EN);
  and and_37 (push_tty, and_32_out, EN);
  and and_38 (halt, and_33_out, EN);
  and and_39 (rnd, and_34_out, EN);
  and and_40 (kbd, and_35_out, EN);
endmodule

module ZeroMapper (
  input  EN,
  input  add,
  input  sub,
  input  mul,
  input  mulu,
  input  div,
  input  divu,
  input  \and ,
  input  \or ,
  input  \nor ,
  input  \xor ,
  input  mfhi,
  input  mflo,
  input  jr,
  input  slt,
  input  sltu,
  output WritePC,
  output [3:0] ALU_SEL,
  output WriteRF,
  output [2:0] RFInput,
  output Unsigned,
  output [1:0] RFSelector,
  output [1:0] BC_SEL
);

  wire AluSel0, AluSel1, AluSel2, AluSel3, or_1_out;

  or or_1 (or_1_out, div, divu);
  or or_2 (AluSel0, sub, sltu, or_1_out, \xor , \or );
  or or_3 (AluSel1, mulu, mul, div, \nor , \xor );
  or or_4 (AluSel2, \nor , \xor , \or , \and );
  or or_5 (AluSel3, slt, sltu);
  assign ALU_SEL = {4{EN}} & {AluSel3, AluSel2, AluSel1, AluSel0};  // AND_Gate and_1, 4 bits wide
  and and_2 (WritePC, EN, 1'b1);
  or or_6 (Unsigned, mulu, divu);
  assign RFSelector = 2'b10 & {2{EN}};  // AND_Gate and_3, 2 bits wide
  and and_4 (BC_SEL[1], jr, EN);
  and and_5 (WriteRF, ~jr, ~mul, ~mulu, ~div, ~divu, EN);  // AND_Gate

  assign BC_SEL[0] = 1'b0;
  assign RFInput = {mfhi, mflo, mfhi};
endmodule

module I_Mapper (
  input  EN,
  input  addi,
  input  andi,
  input  ori,
  input  xori,
  input  slti,
  input  sltiu,
  output WritePC,
  output WriteRF,
  output ALUA,
  output [1:0] ALUB,
  output [2:0] RF_INPUT,
  output [1:0] RF_SEL,
  output [1:0] BC_SEL,
  output [3:0] ALU_SEL
);

  wire AluSel0, AluSel2, AluSel3;

  or or_1 (AluSel0, ori, xori, sltiu);
  or or_2 (AluSel2, andi, ori, xori);
  or or_3 (AluSel3, slti, sltiu);
  and and_1 (WritePC, EN, 1'b1);
  and and_2 (WriteRF, EN, 1'b1);
  or or_4 (ALUB[0], addi, slti, sltiu);
  or or_5 (ALUB[1], andi, ori, xori);
  assign ALU_SEL = {4{EN}} & {AluSel3, AluSel2, xori, AluSel0};  // AND_Gate and_3, 4 bits wide

  assign ALUA = 1'b0;
  assign BC_SEL = 2'b00;
  assign RF_INPUT = 3'b000;
  assign RF_SEL = 2'b00;

  // Other names for the same wires on the sheet: AluSel1 = xori
endmodule

module Get_Instruction (
  input  [5:0] Op_Code,
  input  [5:0] Func_code,
  output [3:0] ALU_SEL,
  output [1:0] B_SEL,
  output stack,
  output [2:0] RF_Input,
  output pop_push,
  output [1:0] RF_SEL,
  output Write_RF
);

  wire add, addi, AluSel0, \and , andi, div, divu, lw, mul, mulu, \nor , \or , or_1_out, or_2_out, or_3_out,
       or_5_out, or_6_out, ori, rnd, slt, slti, sltiu, sltu, sub, sw, \xor , xori, zero;

  Op_Code_Decoder op_code_decoder_1 (
    .o0(Op_Code[0]), .o1(Op_Code[1]), .o2(Op_Code[2]), .o3(Op_Code[3]), .o4(Op_Code[4]), .o5(Op_Code[5]),
    .zero(zero), .addi(addi), .andi(andi), .ori(ori), .xori(xori), .lw(lw), .slti(slti), .sw(sw),
    .sltiu(sltiu), .stack(stack), .ENABLE(1'b1));  // open: beq, special, bne, blez, bgtz, bltz
  Func_Code_Decoder func_code_decoder_1 (
    .f0(Func_code[0]), .f1(Func_code[1]), .f2(Func_code[2]), .f3(Func_code[3]), .f4(Func_code[4]),
    .f5(Func_code[5]), .EN(1'b1), .add(add), .\and (\and ), .sub(sub), .\or (\or ), .push_tty(pop_push),
    .mul(mul), .\nor (\nor ), .mulu(mulu), .\xor (\xor ), .rnd(rnd), .div(div), .mfhi(RF_Input[2]),
    .mflo(RF_Input[1]), .divu(divu), .slt(slt), .sltu(sltu), .zero(zero));  // open: nop_pop, halt, kbd, jr
  or or_1 (or_1_out, div, divu);
  or or_2 (or_2_out, ori, \or );
  or or_3 (or_3_out, \xor , xori);
  or or_4 (RF_Input[0], RF_Input[2], rnd);
  or or_5 (or_5_out, or_2_out, or_3_out);
  or or_6 (or_6_out, \and , andi);
  or or_7 (AluSel0, sub, sltu, or_1_out, or_5_out);
  or or_8 (ALU_SEL[1], mulu, mul, div, \nor , or_3_out);
  or or_9 (ALU_SEL[2], or_6_out, or_3_out, \nor );
  or or_10 (ALU_SEL[3], slt, sltu);
  or or_11 (RF_SEL[1], add, sub, mul, mulu, div, divu, slt, RF_Input[2], RF_Input[1], sltu, \and , \or , \nor , \xor );
  or or_12 (RF_SEL[0], addi, andi, ori, xori, slti, sltiu);
  buf or_13 (B_SEL[0], ori);  // OR_Gate
  or or_14 (B_SEL[1], addi, slti, sltiu);
  or or_15 (Write_RF, RF_SEL[1], RF_SEL[0]);

  assign ALU_SEL[0] = ALU_SEL[1];

  // Other names for the same wires on the sheet: AluSel1 = ALU_SEL[1]; AluSel2 = ALU_SEL[2]; AluSel3 = ALU_SEL[3];
  //   push = pop_push; mflo = RF_Input[1]; mfhi = RF_Input[2]

  // Notes on the sheet:
  //   picking Rd
  //   picking Rt
endmodule

module Branch_Mapper (
  input  beq,
  input  bne,
  input  blez,
  input  bgtz,
  input  bltz,
  output [2:0] Flag_Sel
);

  or or_1 (Flag_Sel[0], blez, bltz);
  or or_2 (Flag_Sel[1], bgtz, bltz);

  assign Flag_Sel[2] = bne;
endmodule
